// Digital circuit Codificador & Decodificador.dig as structural Verilog
module Codificador___Decodificador (
  input  A,
  input  B,
  input  C,
  input  A1,
  input  A2,
  input  A3,
  input  A4,
  input  A5,
  input  A6,
  input  A7,
  output _0,
  output _1,
  output _2,
  output _3,
  output _4,
  output _5,
  output _6,
  output _7,
  output O0,
  output O1,
  output O2
);

  wire not_1_out, not_2_out, not_3_out;

  not not_1 (not_1_out, C);
  not not_2 (not_2_out, B);
  not not_3 (not_3_out, A);
  and and_1 (_0, not_3_out, not_2_out, not_1_out);
  and and_2 (_1, A, not_2_out, not_1_out);
  and and_3 (_2, not_3_out, B, not_1_out);
  and and_4 (_3, A, B, not_1_out);
  and and_5 (_4, not_3_out, not_2_out, C);
  and and_6 (_5, A, not_2_out, C);
  and and_7 (_6, not_3_out, B, C);
  and and_8 (_7, A, B, C);
  or or_1 (O0, A1, A3, A5, A7);
  or or_2 (O1, A2, A3, A6, A7);
  or or_3 (O2, A4, A5, A6, A7);
endmodule

/* Test case Teste Decodificador:
A	B	C	0	1	2	3	4	5	6	7
0	0	0	1	0	0	0	0	0	0	0
1	0	0	0	1	0	0	0	0	0	0
0	1	0	0	0	1	0	0	0	0	0
1	1	0	0	0	0	1	0	0	0	0
0	0	1	0	0	0	0	1	0	0	0
1	0	1	0	0	0	0	0	1	0	0
0	1	1	0	0	0	0	0	0	1	0
1	1	1	0	0	0	0	0	0	0	1	
*/

/* Test case Teste Codificador:
1	2	3	4	5	6	7	A	B	C
0	0	0	0	0	0	0	0	0	0
1	0	0	0	0	0	0	1	0	0
0	1	0	0	0	0	0	0	1	0
0	0	1	0	0	0	0	1	1	0
0	0	0	1	0	0	0	0	0	1
0	0	0	0	1	0	0	1	0	1
0	0	0	0	0	1	0	0	1	1
0	0	0	0	0	0	1	1	1	1
*/
