// Digital circuit Lab 3.dig as structural Verilog
module Lab_3 (
  input  A0,
  input  A1,
  input  A2,
  input  A3,
  input  Control,
  input  Data,
  output Memory
);

  wire and_1_out, and_2_out, not_1_out;

  not not_1 (not_1_out, A1);
  and and_1 (and_1_out, A0, not_1_out, A2, A3);
  and and_2 (and_2_out, and_1_out, Control);
  D_FF d_ff_1 (.D(Data), .C(and_2_out), .Q(Memory));  // open: nQ
endmodule

/* Test case:
A0 A1 A2 A3 Memory Control Data
1  0  1  1  0      0       0
1  0  1  1  1      1       1
0  0  1  1  1      1       0
1  0  1  1  1      0       0
1  0  1  1  0      1       0
*/
