// Digital circuit Decodificador.dig as structural Verilog
module Decodificador (
  input  A,
  input  B,
  input  C,
  output _0,
  output _1,
  output _2,
  output _3,
  output _4,
  output _5,
  output _6,
  output _7
);

  wire not_1_out, not_2_out, not_3_out;

  not not_1 (not_1_out, C);
  not not_2 (not_2_out, B);
  not not_3 (not_3_out, A);
  and and_1 (_0, not_3_out, not_2_out, not_1_out);
  and and_2 (_1, A, not_2_out, not_1_out);
  and and_3 (_2, not_3_out, B, not_1_out);
  and and_4 (_3, A, B, not_1_out);
  and and_5 (_4, not_3_out, not_2_out, C);
  and and_6 (_5, A, not_2_out, C);
  and and_7 (_6, not_3_out, B, C);
  and and_8 (_7, A, B, C);
endmodule

/* Test case Teste Codificador:
A	B	C	0	1	2	3	4	5	6	7
0	0	0	1	0	0	0	0	0	0	0
1	0	0	0	1	0	0	0	0	0	0
0	1	0	0	0	1	0	0	0	0	0
1	1	0	0	0	0	1	0	0	0	0
0	0	1	0	0	0	0	1	0	0	0
1	0	1	0	0	0	0	0	1	0	0
0	1	1	0	0	0	0	0	0	1	0
1	1	1	0	0	0	0	0	0	0	1	
*/
