// Digital circuit Máquina de Estado.dig as structural Verilog
module \Máquina_de_Estado  (
  input  clk,
  input  in_2,
  output Q0,
  output Q1
);

  wire and_1_out, and_2_out, and_3_out, d_ff_1_nq, d_ff_2_nq, not_1_out, or_1_out, or_2_out;

  and and_1 (and_1_out, in_2, or_1_out);
  or or_1 (or_1_out, Q0, Q1);
  D_FF d_ff_1 (.D(and_1_out), .C(clk), .Q(Q1), .nQ(d_ff_1_nq));
  and and_2 (and_2_out, not_1_out, Q1);
  not not_1 (not_1_out, in_2);
  and and_3 (and_3_out, in_2, d_ff_1_nq, d_ff_2_nq);
  or or_2 (or_2_out, and_2_out, and_3_out);
  D_FF d_ff_2 (.D(or_2_out), .C(clk), .Q(Q0), .nQ(d_ff_2_nq));
endmodule
