// Digital circuit ULA.dig as structural Verilog
module ULA (
  input  A,
  input  B,
  input  CarryIn,
  input  B0,
  input  A0,
  input  B2,
  input  A2,
  input  B1,
  input  A1,
  input  B3,
  input  A3,
  output Soma,
  output CarryOut,
  output S0,
  output S1,
  output S2,
  output S3,
  output Cout
);

  wire add_2_c_o, add_3_c_o, add_4_c_o, and_1_out, and_2_out, and_3_out, xor_1_out;

  Add add_1 (.a(A3), .b(B3), .c_i(add_2_c_o), .s(S3), .c_o(Cout));
  Add add_2 (.a(A2), .b(B2), .c_i(add_3_c_o), .s(S2), .c_o(add_2_c_o));
  xor xor_1 (xor_1_out, A, B);
  and and_1 (and_1_out, CarryIn, B);
  and and_2 (and_2_out, CarryIn, A);
  and and_3 (and_3_out, B, A);
  Add add_3 (.a(A1), .b(B1), .c_i(add_4_c_o), .s(S1), .c_o(add_3_c_o));
  Add add_4 (.a(A0), .b(B0), .c_i(1'b0), .s(S0), .c_o(add_4_c_o));
  xor xor_2 (Soma, xor_1_out, CarryIn);
  or or_1 (CarryOut, and_1_out, and_2_out, and_3_out);
endmodule

/* Test case ULA:
A	B	CarryIn	Soma	CarryOut
0	0	0	0	0
0	0	1	1	0
0	1	0	1	0
0	1	1	0	1
1	0	0	1	0
1	0	1	0	1
1	1	0	0	1
1	1	1	1	1
*/
